// Logisim project olaf2.circ as structural Verilog: 6 circuits, main circuit main
module main (
  input  RST
);

  wire CLK_out, cpu_1_get, cpu_1_out, cpu_1_ram_ld, cpu_1_ram_str, cpu_1_rst_out_2, not_1_out, RST_out;
  wire [6:0] keyboard_1_data;
  wire [15:0] bit_extender_1_out, cpu_1_ip, cpu_1_ram_store, cpu_1_rst_out, cpu_1_sp, ram_1_data;
  wire [23:0] rom_1_data;

  Clock CLK (.out(CLK_out));
  or u_RST (RST_out, cpu_1_rst_out_2, RST);
  Pull_Resistor pull_resistor_1 (.node(RST));
  CPU cpu_1 (
    .CLK(CLK_out), .RST_IN(RST), .OPCODE(rom_1_data), .IP(cpu_1_ip), .RST_OUT_2(cpu_1_rst_out_2),
    .RST_OUT(cpu_1_rst_out[0]), .IN(bit_extender_1_out), .OUT(cpu_1_out), .GET(cpu_1_get), .SP(cpu_1_sp),
    .RAM_STORE(cpu_1_ram_store), .RAM_LOAD(ram_1_data), .RAM_STR(cpu_1_ram_str), .RAM_LD(cpu_1_ram_ld));
  ROM #(.addrWidth(16), .dataWidth(24)) rom_1 (.addr(cpu_1_ip), .data(rom_1_data), .sel(1'b1));
  RAM #(.addrWidth(16), .dataWidth(16), .bus("separate")) ram_1 (
    .addr(cpu_1_sp), .din(cpu_1_ram_store), .data(ram_1_data), .str(cpu_1_ram_str), .sel(1'b1),
    .clk(CLK_out), .ld(cpu_1_ram_ld), .clr(RST_out));
  Pull_Resistor pull_resistor_2 (.node(ram_1_data));
  TTY #(.rows(16), .cols(64)) tty_1 (.data(cpu_1_rst_out[6:0]), .clk(CLK_out), .we(cpu_1_out), .clr(RST_out));
  not not_1 (not_1_out, CLK_out);
  Keyboard #(.buflen(256)) keyboard_1 (
    .clk(not_1_out), .re(cpu_1_get), .clr(RST_out), .data(keyboard_1_data));  // open: avail
  assign bit_extender_1_out = {{9{1'b0}}, keyboard_1_data};  // Bit_Extender bit_extender_1
  // Pins of 1 and 16 bits meet at cpu_1_rst_out

  // Notes on the sheet:
  //   contents of rom_1 (hex, n*v repeats v):
  //   1d11 5c 7c 9c bc 3c fc 3d 621 1c f 722 10 1d 3d 3e2 1e 1d fc 3d 721 10 1d 3d bd 9d 7d 5d 1e 12e1b 9a
  //   ef1b a19 79a ef1b 1409a d71b 1409a ef1b 4019 9a ef1b 2319 2019 1c09a d71b 1c09a 122ba fa1b 10c 6212
  //   1c09a 11bba fa1b 10c 6712 1c09a 12bba fa1b 10c 6612 1c09a 112ba fa1b 10c 6412 1c09a 13bba fa1b 10c
  //   6b12 1c09a 118ba fa1b 10c 6912 1c09a 138ba fa1b 10c 2112 1c09a 131ba fa1b 10c 6d12 1c03a 2f 2c 6112
  //   1c09a ef1b 3a19 2019 329a ef1b a19 2511 861b 2511 8e1b 2511 811b 6f1b 2511 971b 2511 aa1b 2511 881b
  //   2511 11b 5a 1891b e 20c d 7f12 5c 9d 1811b 1c 9d ef1b a19 141 7111 111b 1e 6219 7919 6219 a19 1d11
  //   c19 1e 11b 1409a ef1b a19 111b 1e 11b 449a ef1b 2409a d71b 2409a 1351b 111b 1e 11b 449a ef1b 2409a
  //   d71b 2409a 14a1b ffff0c a612 2409a ef1b 299a ef1b a19 1e 1039a ef1b 111b 1e 559a ef1b a19 5f9a ef1b
  //   a19 859a ef1b a19 9f9a ef1b a19 b79a ef1b a19 db9a ef1b a19 ec9a ef1b a19 1e 3e19 9c 3409a d71b 9d
  //   2119 16*0 1e 9c 3d 1a 78 6c da12 86c e612 19 a6c ec12 70 121 101 da11 c da12 122 102 19 da11 7a 70
  //   1e 11b 9c 3d 6f 6c f812 19 121 f211 111b 1e 5c 9c 3d f 181 bc 3d 4f 1a1 e 20c d 10c13 c 10a12 fb11
  //   11a 10e11 1a 10e11 5d 1e 9c bc 9c 3d f bc 3d 10 c 11d12 181 1a1 11211 bd 9d 1e 5c 9c 11a 9c 3d 4f 4c
  //   12b12 101 181 12311 9d 5d 1e 34b3a 54d1a 10 34c3a 144d1a 10 1e 11b 34b3a af 1101b 34a3a 8f 1971b 1c
  //   3d b0 34b3a 8f 1201b e 401 d 34b3a 10 18c1b 111b 1e 11b 1631b ffff0c c01b 16112 7c 1c 7d 1e61 19 7d
  //   1c 9d 1971b 3c 1c 3d 1a 10 121 10 11a 3d 111b 1e 11b 9c bd 5a 1891b e 20c d 17912 5c 9d 1811b 1c 9d
  //   fa1b 10c 17612 141 16711 5c 1d 17b11 4e19 ffff1a 111b 1e 9c 1d 101 1e 1971b 1c 3d f 1e 1971b 101 1e
  //   34a3a f 1e 9c 1c 1c 9d 1891b 101 34a3a 10 1d 9d 1e 9c 283 34d81 9c 1d 9d 1e
endmodule

module ALU (
  input  [15:0] SOURCE,
  input  [15:0] DEST,
  input  ADD,
  input  SUB,
  input  MUL,
  input  DIV,
  input  SHL,
  input  SHR,
  input  NOT,
  input  AND,
  input  OR,
  input  XOR,
  output ZERO,
  output CARRY,
  output [15:0] MOD,
  output [15:0] OUT,
  output [15:0] MOD_2,
  output CARRY_2
);

  wire not_1_out, not_2_out, not_3_out, not_4_out, not_5_out, not_6_out, not_7_out, not_8_out, not_9_out,
       not_10_out, not_11_out, not_12_out, not_13_out, not_14_out, not_15_out, not_16_out;
  wire [3:0] controlled_buffer_12_out, pull_resistor_4_node;
  wire [15:0] adder_1_out, and_1_out, controlled_buffer_1_out, controlled_buffer_2_out,
       controlled_buffer_3_out, controlled_buffer_5_out, controlled_buffer_6_out, controlled_buffer_7_out,
       controlled_buffer_8_out, controlled_buffer_11_out, controlled_buffer_13_out, controlled_buffer_15_out,
       controlled_buffer_16_out, controlled_buffer_17_out, controlled_buffer_19_out, divider_1_out,
       multiplier_1_out, or_2_out, OUT_out, pull_resistor_2_node, pull_resistor_3_node, pull_resistor_8_node,
       pull_resistor_12_node, shifter_1_out, shifter_2_out, subtractor_1_out, xor_1_out;

  or or_1 (CARRY_2, ADD, SUB, MUL, DIV, SHL, SHR, NOT, AND, OR, XOR);
  assign controlled_buffer_1_out = ADD ? SOURCE : 16'bz;  // Controlled_Buffer controlled_buffer_1
  assign controlled_buffer_2_out = ADD ? DEST : 16'bz;  // Controlled_Buffer controlled_buffer_2
  assign controlled_buffer_3_out = SUB ? SOURCE : 16'bz;  // Controlled_Buffer controlled_buffer_3
  Pull_Resistor pull_resistor_1 (.node(controlled_buffer_3_out));
  Pull_Resistor pull_resistor_2 (.node(pull_resistor_2_node));
  assign pull_resistor_2_node = SUB ? DEST : 16'bz;  // Controlled_Buffer controlled_buffer_4
  assign controlled_buffer_5_out = MUL ? SOURCE : 16'bz;  // Controlled_Buffer controlled_buffer_5
  assign controlled_buffer_6_out = MUL ? DEST : 16'bz;  // Controlled_Buffer controlled_buffer_6
  assign controlled_buffer_7_out = DIV ? SOURCE : 16'bz;  // Controlled_Buffer controlled_buffer_7
  assign controlled_buffer_8_out = DIV ? DEST : 16'bz;  // Controlled_Buffer controlled_buffer_8
  Pull_Resistor pull_resistor_3 (.node(pull_resistor_3_node));
  assign pull_resistor_3_node = SHL ? SOURCE : 16'bz;  // Controlled_Buffer controlled_buffer_9
  Pull_Resistor pull_resistor_4 (.node(pull_resistor_4_node));
  assign pull_resistor_4_node = SHL ? DEST[3:0] : 4'bz;  // Controlled_Buffer controlled_buffer_10
  assign controlled_buffer_11_out = SHR ? SOURCE : 16'bz;  // Controlled_Buffer controlled_buffer_11
  Pull_Resistor pull_resistor_5 (.node(controlled_buffer_11_out));
  assign controlled_buffer_12_out = SHR ? DEST[3:0] : 4'bz;  // Controlled_Buffer controlled_buffer_12
  Pull_Resistor pull_resistor_6 (.node(controlled_buffer_12_out));
  assign controlled_buffer_13_out = NOT ? SOURCE : 16'bz;  // Controlled_Buffer controlled_buffer_13
  Pull_Resistor #(.pull(1)) pull_resistor_7 (.node(controlled_buffer_13_out));
  Pull_Resistor pull_resistor_8 (.node(pull_resistor_8_node));
  assign pull_resistor_8_node = AND ? SOURCE : 16'bz;  // Controlled_Buffer controlled_buffer_14
  assign controlled_buffer_15_out = AND ? DEST : 16'bz;  // Controlled_Buffer controlled_buffer_15
  Pull_Resistor pull_resistor_9 (.node(controlled_buffer_15_out));
  assign controlled_buffer_16_out = OR ? SOURCE : 16'bz;  // Controlled_Buffer controlled_buffer_16
  Pull_Resistor pull_resistor_10 (.node(controlled_buffer_16_out));
  assign controlled_buffer_17_out = OR ? DEST : 16'bz;  // Controlled_Buffer controlled_buffer_17
  Pull_Resistor pull_resistor_11 (.node(controlled_buffer_17_out));
  Pull_Resistor pull_resistor_12 (.node(pull_resistor_12_node));
  assign pull_resistor_12_node = XOR ? SOURCE : 16'bz;  // Controlled_Buffer controlled_buffer_18
  assign controlled_buffer_19_out = XOR ? DEST : 16'bz;  // Controlled_Buffer controlled_buffer_19
  Pull_Resistor pull_resistor_13 (.node(controlled_buffer_19_out));
  Adder #(.width(16), .value('h0)) adder_1 (
    .a(controlled_buffer_1_out), .b(controlled_buffer_2_out), .out(adder_1_out), .cout(CARRY));  // open: cin
  Subtractor #(.width(16)) subtractor_1 (
    .a(controlled_buffer_3_out), .b(pull_resistor_2_node), .out(subtractor_1_out), .bin(1'b0), .bout(MOD[0]));
  Multiplier #(.width(16), .shift("lr")) multiplier_1 (
    .a(controlled_buffer_5_out), .b(controlled_buffer_6_out), .out(multiplier_1_out), .cin({16{1'b0}}));  // open: cout
  Divider #(.width(16)) divider_1 (
    .a(controlled_buffer_7_out), .b(controlled_buffer_8_out), .out(divider_1_out), .upper({16{1'b0}}),
    .rem(MOD_2));
  Shifter #(.width(16)) shifter_1 (.in(pull_resistor_3_node), .\dist (pull_resistor_4_node), .out(shifter_1_out));
  Shifter #(.width(16), .shift("lr")) shifter_2 (
    .in(controlled_buffer_11_out), .\dist (controlled_buffer_12_out), .out(shifter_2_out));
  assign OUT_out = ~controlled_buffer_13_out;  // NOT_Gate OUT, 16 bits wide
  assign and_1_out = pull_resistor_8_node & controlled_buffer_15_out;  // AND_Gate and_1, 16 bits wide
  assign or_2_out = controlled_buffer_16_out | controlled_buffer_17_out;  // OR_Gate or_2, 16 bits wide
  assign xor_1_out = pull_resistor_12_node ^ controlled_buffer_19_out;  // XOR_Gate xor_1, 16 bits wide
  Pull_Resistor pull_resistor_14 (.node(adder_1_out));
  Pull_Resistor pull_resistor_15 (.node(multiplier_1_out));
  Pull_Resistor pull_resistor_16 (.node(divider_1_out));
  Pull_Resistor pull_resistor_17 (.node(shifter_1_out));
  Pull_Resistor pull_resistor_18 ();  // open: node
  Pull_Resistor pull_resistor_19 (.node(OUT_out));
  Pull_Resistor pull_resistor_20 (.node(and_1_out));
  Pull_Resistor pull_resistor_21 (.node(or_2_out));
  Pull_Resistor pull_resistor_22 (.node(xor_1_out));
  Pull_Resistor pull_resistor_23 (.node(CARRY));
  Pull_Resistor pull_resistor_24 (.node(MOD));
  ExactlyOne xor_2[15:0] (
    .out(OUT), .in0(adder_1_out), .in1(subtractor_1_out), .in2(multiplier_1_out), .in3(divider_1_out),
    .in4(shifter_1_out), .in5(shifter_2_out), .in6(OUT_out), .in7(and_1_out), .in8(or_2_out), .in9(xor_1_out));
  Pull_Resistor pull_resistor_25 (.node(MOD_2));
  Pull_Resistor pull_resistor_26 (.node(OUT));
  not not_1 (not_1_out, OUT[0]);
  not not_2 (not_2_out, OUT[1]);
  not not_3 (not_3_out, OUT[2]);
  not not_4 (not_4_out, OUT[3]);
  not not_5 (not_5_out, OUT[4]);
  not not_6 (not_6_out, OUT[5]);
  not not_7 (not_7_out, OUT[6]);
  not not_8 (not_8_out, OUT[7]);
  not not_9 (not_9_out, OUT[8]);
  not not_10 (not_10_out, OUT[9]);
  not not_11 (not_11_out, OUT[10]);
  not not_12 (not_12_out, OUT[11]);
  not not_13 (not_13_out, OUT[12]);
  not not_14 (not_14_out, OUT[13]);
  not not_15 (not_15_out, OUT[14]);
  not not_16 (not_16_out, OUT[15]);
  and and_2 (ZERO, not_1_out, not_2_out, not_3_out, not_4_out, not_5_out, not_6_out, not_7_out, not_8_out, not_9_out, not_10_out, not_11_out, not_12_out, not_13_out, not_14_out, not_15_out, not_16_out, 1'b1);
  // Pins of 1 and 16 bits meet at MOD
endmodule

module CPU (
  input  [15:0] IN,
  input  CLK,
  input  RST_IN,
  input  [23:0] OPCODE,
  input  [15:0] RAM_LOAD,
  output GET,
  output OUT,
  output RST_OUT,
  output RST_OUT_2,
  output RAM_LD,
  output RAM_STR,
  output [15:0] RAM_STORE,
  output [15:0] IP,
  output [15:0] SP
);

  wire alu_1_carry_2, controlled_buffer_2_out, decoder_1_out1, decoder_1_out2, decoder_1_out3,
       decoder_1_out4, decoder_1_out5, decoder_1_out6, decoder_1_out7, decoder_1_out8, decoder_1_out9,
       decoder_1_out10, decoder_1_out11, decoder_1_out12, decoder_1_out13, decoder_1_out14, decoder_1_out15,
       decoder_1_out16, decoder_1_out17, decoder_1_out18, decoder_1_out19, decoder_1_out20, decoder_1_out21,
       decoder_1_out22, decoder_1_out23, decoder_1_out25, decoder_1_out26, decoder_1_out27, decoder_1_out28,
       decoder_1_out29, decoder_1_out30, DIV_out, flags_1_p1, flags_1_p15, flags_1_p16, flags_1_p18,
       HAS_VALLUE_out, i_o_1_prnt, JMP_out, MOV_2_out, MOV_out, nor_1_out, not_1_out, not_2_out, not_3_out,
       not_4_out, not_5_out, PRT_out, PSH_out, RST_2_out, RST_out_3;
  wire [2:0] flags_1_p17, i_o_1_data_reg, REG_out;
  wire [15:0] alu_1_mod_2, alu_1_out, controlled_buffer_1_out, controlled_buffer_3_out,
       controlled_buffer_4_out, controlled_buffer_5_out, controlled_buffer_7_out, controlled_buffer_8_p3,
       controlled_buffer_9_out, controlled_buffer_10_out, DST_out, flags_1_p14, i_o_1__in, or_1_out,
       pull_resistor_4_node, pull_resistor_7_node, regs_1_ra, regs_1_rb, regs_1_rc, regs_1_rd, regs_1_rdi,
       regs_1_rsi, regs_1_sp, VAL_out;
  wire [15:1] pull_resistor_8_node;

  Decoder #(.select(5), .enable("false")) decoder_1 (
    .out1(decoder_1_out1), .out2(decoder_1_out2), .out3(decoder_1_out3), .out4(decoder_1_out4),
    .out5(decoder_1_out5), .out6(decoder_1_out6), .out7(decoder_1_out7), .out8(decoder_1_out8),
    .out9(decoder_1_out9), .out10(decoder_1_out10), .out11(decoder_1_out11), .out12(decoder_1_out12),
    .out13(decoder_1_out13), .out14(decoder_1_out14), .out15(decoder_1_out15), .out16(decoder_1_out16),
    .out17(decoder_1_out17), .out18(decoder_1_out18), .out19(decoder_1_out19), .out20(decoder_1_out20),
    .out21(decoder_1_out21), .out22(decoder_1_out22), .out23(decoder_1_out23), .out24(GET),
    .out25(decoder_1_out25), .out26(decoder_1_out26), .out27(decoder_1_out27), .out28(decoder_1_out28),
    .out29(decoder_1_out29), .out30(decoder_1_out30), .out31(RST_OUT_2), .sel(OPCODE[4:0]));  // open: out0
  or RST (RST_out_3, RST_OUT_2, RST_IN);
  Pull_Resistor pull_resistor_1 (.node(RAM_LOAD));
  or PRT (PRT_out, decoder_1_out2, decoder_1_out12);
  or JMP (JMP_out, decoder_1_out17, decoder_1_out30, decoder_1_out27);
  or PSH (PSH_out, decoder_1_out27, decoder_1_out28);
  assign REG_out = flags_1_p17 | i_o_1_data_reg | OPCODE[7:5];  // OR_Gate REG, 3 bits wide
  assign controlled_buffer_1_out = RST_2_out ? OPCODE[23:8] : 16'bz;  // Controlled_Buffer controlled_buffer_1
  Pull_Resistor pull_resistor_2 (.node(controlled_buffer_1_out));
  or RST_2 (RST_2_out, decoder_1_out26, flags_1_p18);
  or HAS_VALLUE (HAS_VALLUE_out, OPCODE[8], OPCODE[9], OPCODE[10], OPCODE[11], OPCODE[12], OPCODE[13], OPCODE[14], OPCODE[15], 1'b0);
  // FLAGS flags_1: pin names not known; wires that end beside it: flags_1_p1, JMP_out, decoder_1_out18, decoder_1_out19, decoder_1_out20, decoder_1_out21, decoder_1_out22, decoder_1_out23, decoder_1_out12, decoder_1_out14, CLK, decoder_1_out13, RST_out_3, flags_1_p14, flags_1_p15, flags_1_p16, flags_1_p17, flags_1_p18
  or MOV (MOV_out, decoder_1_out26, flags_1_p18, decoder_1_out15, MOV_2_out, GET);
  assign VAL_out = controlled_buffer_1_out | i_o_1__in | or_1_out | RAM_LOAD;  // OR_Gate VAL, 16 bits wide
  assign controlled_buffer_2_out = decoder_1_out25 ? HAS_VALLUE_out : 1'bz;  // Controlled_Buffer controlled_buffer_2
  not not_1 (not_1_out, flags_1_p1);
  assign controlled_buffer_3_out = not_1_out ? OPCODE[23:8] : 16'bz;  // Controlled_Buffer controlled_buffer_3
  or DIV (DIV_out, decoder_1_out4, decoder_1_out5);
  I_O i_o_1 (
    .GET(GET), .OUT_2(decoder_1_out25), .IN_2(IN), ._IN(i_o_1__in), .PRNT(i_o_1_prnt),
    .DATA_REG(i_o_1_data_reg));
  REGS regs_1 (
    .CLK(CLK), .RST(RST_out_3), .REG(REG_out), .VAL(VAL_out), .MOV(MOV_out), .RA(regs_1_ra), .RB(regs_1_rb),
    .RC(regs_1_rc), .RD(regs_1_rd), .SP(regs_1_sp), .PUSH(PSH_out), .POP(decoder_1_out29),
    .RET(decoder_1_out30), .RDI(regs_1_rdi), .RSI(regs_1_rsi), .IP(IP));
  Pull_Resistor pull_resistor_3 (.node(controlled_buffer_2_out));
  Pull_Resistor pull_resistor_4 (.node(pull_resistor_4_node));
  assign DST_out = pull_resistor_4_node | controlled_buffer_3_out;  // OR_Gate DST, 16 bits wide
  Pull_Resistor pull_resistor_5 (.node(controlled_buffer_3_out));
  assign controlled_buffer_4_out = not_2_out ? controlled_buffer_5_out : 16'bz;  // Controlled_Buffer controlled_buffer_4
  assign controlled_buffer_5_out = i_o_1_prnt ? regs_1_rd : 16'bz;  // Controlled_Buffer controlled_buffer_5
  Pull_Resistor pull_resistor_6 (.node(controlled_buffer_4_out));
  not not_2 (not_2_out, controlled_buffer_2_out);
  Pull_Resistor pull_resistor_7 (.node(pull_resistor_7_node));
  assign pull_resistor_7_node = controlled_buffer_2_out ? OPCODE[23:8] : 16'bz;  // Controlled_Buffer controlled_buffer_6
  ALU alu_1 (
    .SOURCE(RAM_STORE), .DEST(DST_out), .ADD(decoder_1_out1), .SUB(PRT_out), .MUL(decoder_1_out3),
    .DIV(DIV_out), .SHL(decoder_1_out6), .SHR(decoder_1_out7), .NOT(decoder_1_out9), .AND(decoder_1_out10),
    .OR(decoder_1_out11), .XOR(decoder_1_out8), .CARRY(flags_1_p15), .MOD(flags_1_p14), .ZERO(flags_1_p16),
    .OUT(alu_1_out), .MOD_2(alu_1_mod_2), .CARRY_2(alu_1_carry_2));
  not not_3 (not_3_out, decoder_1_out12);
  Pull_Resistor pull_resistor_8 (.node({pull_resistor_8_node, RST_OUT}));
  Pull_Resistor pull_resistor_9 (.node({pull_resistor_8_node, RST_OUT}));
  assign {pull_resistor_8_node, RST_OUT} = controlled_buffer_4_out | pull_resistor_7_node;  // OR_Gate PRT_2, 16 bits wide
  and MOV_2 (MOV_2_out, alu_1_carry_2, not_3_out);
  assign controlled_buffer_7_out = decoder_1_out5 ? alu_1_mod_2 : 16'bz;  // Controlled_Buffer controlled_buffer_7
  Pull_Resistor pull_resistor_10 (.node(controlled_buffer_7_out));
  Multiplexer #(.select(3), .width(16), .enable("false")) multiplexer_1 (
    .in0(regs_1_ra), .in1(regs_1_rb), .in2(regs_1_rc), .in3(regs_1_rd), .in4(regs_1_rdi), .in5(regs_1_rsi),
    .in6(IP), .in7(regs_1_sp), .out(RAM_STORE), .sel(REG_out));
  nor nor_1 (nor_1_out, decoder_1_out15, decoder_1_out16);
  // Controlled_Buffer #(.width(16)) controlled_buffer_8: pin names not known; wires that end beside it: regs_1_sp, nor_1_out, controlled_buffer_8_p3
  Multiplexer #(.select(3), .width(16)) multiplexer_2 (
    .in0(regs_1_ra), .in1(regs_1_rb), .in2(regs_1_rc), .in3(regs_1_rd), .in4(regs_1_rdi), .in5(regs_1_rsi),
    .in6(IP), .in7(regs_1_sp), .out(pull_resistor_4_node), .sel(OPCODE[10:8]), .en(flags_1_p1));
  DotMatrix #(.matrixcols(4), .matrixrows(16)) dotmatrix_1 (
    .col0(RAM_STORE), .col1(OPCODE[23:8]), .col2(alu_1_out), .col3(alu_1_mod_2));
  not not_4 (not_4_out, decoder_1_out5);
  assign controlled_buffer_9_out = not_4_out ? alu_1_out : 16'bz;  // Controlled_Buffer controlled_buffer_9
  Pull_Resistor pull_resistor_11 (.node(controlled_buffer_9_out));
  assign or_1_out = controlled_buffer_7_out | controlled_buffer_9_out;  // OR_Gate or_1, 16 bits wide
  Pull_Resistor pull_resistor_12 (.node(or_1_out));
  or or_2 (OUT, RST_OUT, pull_resistor_8_node[1], pull_resistor_8_node[2], pull_resistor_8_node[3], pull_resistor_8_node[4], pull_resistor_8_node[5], pull_resistor_8_node[6]);
  not not_5 (not_5_out, nor_1_out);
  assign controlled_buffer_10_out = not_5_out ? regs_1_rb : 16'bz;  // Controlled_Buffer controlled_buffer_10
  or or_3 (RAM_LD, decoder_1_out29, decoder_1_out15, decoder_1_out30);
  or or_4 (RAM_STR, PSH_out, decoder_1_out16);
  Pull_Resistor pull_resistor_13 (.node(RAM_STORE));
  Pull_Resistor pull_resistor_14 (.node(controlled_buffer_10_out));
  assign SP = controlled_buffer_10_out | controlled_buffer_8_p3;  // OR_Gate or_5, 16 bits wide
  Pull_Resistor pull_resistor_15 (.node(controlled_buffer_8_p3));
  // Pins of 1 and 16 bits meet at {pull_resistor_8_node, RST_OUT}

  // Notes on the sheet:
  //   IN: pull=down
  //   OPCODE: pull=down
  //   RAM_LOAD: pull=down
  //   NOP
  //   ADD
  //   MUL
  //   DIV
  //   MOD
  //   SHL
  //   SHR
  //   XOR
  //   NOT
  //   AND
  //   OR
  //   TEST
  //   CHDC
  //   CHDR
  //   LOAD
  //   STOR
  //   JMP
  //   JEQ
  //   JNE
  //   JBT
  //   JST
  //   JBE
  //   JLE
  //   GET
  //   OUT
  //   MOV
  //   CALL
  //   PUSH
  //   POP
  //   RET
  //   RST
  //   RST
  //   SRC
endmodule

module REGS (
  input  CLK,
  input  RST,
  input  [2:0] REG,
  input  [15:0] VAL,
  input  MOV,
  input  PUSH,
  input  POP,
  input  RET,
  output [15:0] RA,
  output [15:0] RB,
  output [15:0] RC,
  output [15:0] RD,
  output [15:0] RDI,
  output [15:0] RSI,
  output [15:0] IP,
  output [15:0] SP
);

  wire decoder_1_out0, decoder_1_out1, decoder_1_out2, decoder_1_out3, decoder_1_out4, decoder_1_out5,
       decoder_1_out6, decoder_1_out7, nor_1_out, not_1_out, not_2_out, not_3_out, not_4_out, or_1_out,
       or_4_out, or_6_out;
  wire [2:0] controlled_buffer_3_out, or_3_out, pull_resistor_4_node;
  wire [15:0] adder_1_out, adder_2_out, controlled_buffer_1_out, controlled_buffer_5_out,
       controlled_buffer_6_out, controlled_buffer_8_out, or_2_out, or_5_out, pull_resistor_2_node,
       pull_resistor_7_node, SP_q, subtractor_1_out;

  not not_1 (not_1_out, RET);
  Decoder #(.select(3), .disabled(0)) decoder_1 (
    .out0(decoder_1_out0), .out1(decoder_1_out1), .out2(decoder_1_out2), .out3(decoder_1_out3),
    .out4(decoder_1_out4), .out5(decoder_1_out5), .out6(decoder_1_out6), .out7(decoder_1_out7),
    .sel(or_3_out), .en(or_1_out));
  or or_1 (or_1_out, MOV, POP);
  assign controlled_buffer_1_out = not_1_out ? VAL : 16'bz;  // Controlled_Buffer controlled_buffer_1
  Pull_Resistor pull_resistor_1 (.node(controlled_buffer_1_out));
  Adder #(.width(16)) adder_1 (.a(VAL), .b(16'h1), .out(adder_1_out), .cin(1'b0));  // open: cout
  Pull_Resistor pull_resistor_2 (.node(pull_resistor_2_node));
  assign pull_resistor_2_node = RET ? adder_1_out : 16'bz;  // Controlled_Buffer controlled_buffer_2
  assign controlled_buffer_3_out = not_2_out ? REG : 3'bz;  // Controlled_Buffer controlled_buffer_3
  Pull_Resistor pull_resistor_3 (.node(controlled_buffer_3_out));
  not not_2 (not_2_out, PUSH);
  Pull_Resistor pull_resistor_4 (.node(pull_resistor_4_node));
  assign pull_resistor_4_node = PUSH ? 3'b110 : 3'bz;  // Controlled_Buffer controlled_buffer_4
  assign or_2_out = controlled_buffer_1_out | pull_resistor_2_node;  // OR_Gate or_2, 16 bits wide
  Register #(.width(16), .trigger("falling")) u_RA (.D(or_2_out), .en(decoder_1_out0), .Q(RA), .clk(CLK), .clr(RST));
  assign or_3_out = controlled_buffer_3_out | pull_resistor_4_node;  // OR_Gate or_3, 3 bits wide
  Register #(.width(16), .trigger("falling")) u_RB (.D(or_2_out), .en(decoder_1_out1), .Q(RB), .clk(CLK), .clr(RST));
  Pull_Resistor pull_resistor_5 (.node(RET));
  Register #(.width(16), .trigger("falling")) u_RD (.D(or_2_out), .en(decoder_1_out2), .Q(RC), .clk(CLK), .clr(RST));
  or or_4 (or_4_out, POP, RET);
  Register #(.width(16), .trigger("falling")) u_RDI (.D(or_2_out), .en(decoder_1_out4), .Q(RDI), .clk(CLK), .clr(RST));
  Register #(.width(16), .trigger("falling")) RD_2 (.D(or_2_out), .en(decoder_1_out3), .Q(RD), .clk(CLK), .clr(RST));
  Register #(.width(16), .trigger("falling")) u_RSI (.D(or_2_out), .en(decoder_1_out5), .Q(RSI), .clk(CLK), .clr(RST));
  not not_3 (not_3_out, decoder_1_out6);
  Subtractor #(.width(16)) subtractor_1 (.a(SP_q), .b(16'h1), .out(subtractor_1_out), .bin(1'b0));  // open: bout
  Adder #(.width(16)) adder_2 (.a(SP_q), .b(16'h1), .out(adder_2_out), .cin(1'b0));  // open: cout
  Pull_Resistor pull_resistor_6 (.node(IP));
  nor nor_1 (nor_1_out, PUSH, or_4_out);
  Counter #(.width(16), .max('hffff), .ongoal("stay"), .trigger("falling")) u_IP (
    .load(decoder_1_out6), .D(or_2_out), .count(not_3_out), .Q(IP), .clk(CLK), .clr(RST));  // open: carry
  assign controlled_buffer_5_out = PUSH ? subtractor_1_out : 16'bz;  // Controlled_Buffer controlled_buffer_5
  assign controlled_buffer_6_out = or_4_out ? adder_2_out : 16'bz;  // Controlled_Buffer controlled_buffer_6
  Pull_Resistor pull_resistor_7 (.node(pull_resistor_7_node));
  assign pull_resistor_7_node = nor_1_out ? or_2_out : 16'bz;  // Controlled_Buffer controlled_buffer_7
  Pull_Resistor pull_resistor_8 (.node(controlled_buffer_5_out));
  assign or_5_out = pull_resistor_7_node | controlled_buffer_5_out | controlled_buffer_6_out;  // OR_Gate or_5, 16 bits wide
  Pull_Resistor pull_resistor_9 (.node(controlled_buffer_6_out));
  or or_6 (or_6_out, decoder_1_out7, or_4_out, PUSH, RET);
  Pull_Resistor pull_resistor_10 (.node(controlled_buffer_5_out));
  Pull_Resistor pull_resistor_11 (.node(controlled_buffer_6_out));
  assign controlled_buffer_8_out = not_4_out ? SP_q : 16'bz;  // Controlled_Buffer controlled_buffer_8
  Register #(.width(16), .trigger("falling")) u_SP (.D(or_5_out), .en(or_6_out), .Q(SP_q), .clk(CLK), .clr(RST));
  Pull_Resistor pull_resistor_12 (.node(controlled_buffer_8_out));
  not not_4 (not_4_out, PUSH);
  assign SP = controlled_buffer_8_out | controlled_buffer_5_out;  // OR_Gate or_7, 16 bits wide

  // Notes on the sheet:
  //   POP: pull=down
  //   PUSH: pull=down
  //   RST: pull=down
  //   RET: pull=down
  //   REG: pull=down
  //   CLK: pull=down
  //   MOV: pull=down
endmodule

module FLAGS (
  input  TEST,
  input  CLK,
  input  RST,
  input  JEQ,
  input  JNE,
  input  JBT,
  input  BORROW,
  input  JST,
  input  CARRY,
  input  JBE,
  input  ZERO,
  input  ZERO_2,
  input  JLE,
  input  JST_2,
  input  CHDC,
  output MOD,
  output JMP_OUT,
  output [2:0] IP_REG,
  output JMP_OUT_2
);

  wire JBE_2_out, JBE_out, JBT_out, JLE_2_out, JLE_3_out, JLE_out, JNE_out, JST_out, not_1_out, not_2_out,
       not_3_out, or_1_out, or_2_out, or_5_out, register_1_q, register_3_q, undriven;

  not not_1 (not_1_out, register_3_q);
  not not_2 (not_2_out, register_1_q);
  and u_JBT (JBT_out, not_2_out, JBT);
  and u_JST (JST_out, register_1_q, JST);
  not not_3 (not_3_out, register_1_q);
  and u_JBE (JBE_out, not_3_out, JBE);
  and JBE_2 (JBE_2_out, register_1_q, JLE);
  and u_JLE (JLE_out, register_1_q, JBE);
  and JLE_2 (JLE_2_out, register_1_q, JLE);
  and JLE_3 (JLE_3_out, JEQ, register_3_q);
  and u_JNE (JNE_out, JNE, not_1_out);
  or or_1 (or_1_out, JBE_out, JLE_out);
  or or_2 (or_2_out, JBE_2_out, JLE_2_out);
  assign IP_REG = JMP_OUT_2 ? 3'b110 : 3'bz;  // Controlled_Buffer controlled_buffer_1
  assign IP_REG = JMP_OUT_2 ? 3'b110 : 3'bz;  // Controlled_Buffer controlled_buffer_2
  Pull_Resistor pull_resistor_1 (.node(IP_REG));
  or or_3 (JMP_OUT_2, undriven, JLE_3_out, JNE_out, JBT_out, JST_out, or_1_out, or_2_out);
  or or_4 (JMP_OUT_2, undriven, JLE_3_out, JNE_out, JBT_out, JST_out, or_1_out, or_2_out);
  Register #(.width(1), .trigger("falling")) register_1 (.D(BORROW), .en(TEST), .Q(register_1_q), .clk(CLK), .clr(RST));
  Register #(.width(1), .trigger("falling")) register_2 (.D(CARRY), .en(TEST), .clk(CLK), .clr(RST));  // open: Q
  Register #(.width(1), .trigger("falling")) register_3 (.D(ZERO), .en(TEST), .Q(register_3_q), .clk(CLK), .clr(RST));
  Register #(.width(1), .trigger("falling")) register_4 (.D(ZERO), .en(TEST), .Q(register_3_q), .clk(CLK), .clr(RST));
  or or_5 (or_5_out, JST_2, CHDC);
  Register #(.width(1), .trigger("falling")) register_5 (.D(JST_2), .en(or_5_out), .Q(MOD), .clk(CLK), .clr(RST));
  // Pins of 1 and 3 bits meet at IP_REG

  assign JMP_OUT = IP_REG[0];
  assign ZERO_2 = ZERO;

  // Notes on the sheet:
  //   CARRY: pull=down
  //   MOD: pull=down
  //   RST: pull=down
  //   ZERO: pull=down
  //   JST: pull=down
  //   CHDC: pull=down
  //   JNE: pull=down
  //   BORROW: pull=down
  //   TEST: pull=down
  //   JBT: pull=down
  //   JEQ: pull=down
  //   JST_2: pull=down
  //   JBE: pull=down
  //   CLK: pull=down
  //   ZERO_2: pull=down
  //   JLE: pull=down
  //   when mod is 0, the ALU will use constant
endmodule

module I_O (
  input  [15:0] IN,
  input  [15:0] IN_2,
  input  GET,
  input  OUT,
  input  OUT_2,
  output [15:0] _IN,
  output PRNT,
  output [2:0] DATA_REG
);

  assign _IN = GET ? IN : 16'bz;  // Controlled_Buffer controlled_buffer_1
  Pull_Resistor pull_resistor_1 (.node(_IN));
  Pull_Resistor pull_resistor_2 (.node(DATA_REG));
  assign DATA_REG = OUT ? 3'b011 : 3'bz;  // Controlled_Buffer controlled_buffer_2

  assign IN_2 = IN;
  assign OUT_2 = OUT;
  assign PRNT = OUT;

  // Notes on the sheet:
  //   OUT: pull=down
  //   IN: pull=down
  //   IN_2: pull=down
  //   GET: pull=down
  //   OUT_2: pull=down
endmodule
